// Digital circuit Punto_3.1.dig as structural Verilog
module Punto_3_1 (
  input  Reset,
  input  Set,
  input  clock,
  output Q,
  output Q_2
);

  wire nand_1_out, nand_2_out, nand_3_out, nand_4_out, nand_5_out, nand_6_out, not_1_out;

  not not_1 (not_1_out, clock);
  nand nand_1 (nand_1_out, Reset, not_1_out);
  nand nand_2 (nand_2_out, not_1_out, Set);
  nand nand_3 (nand_3_out, nand_1_out, nand_4_out);
  nand nand_4 (nand_4_out, nand_3_out, nand_2_out);
  nand nand_5 (nand_5_out, clock, nand_3_out);
  nand nand_6 (nand_6_out, nand_4_out, clock);
  nand nand_7 (Q, nand_5_out, Q_2);
  nand nand_8 (Q_2, Q, nand_6_out);

  // Notes on the sheet:
  //   Set: default 1
  //   Los flip flop RS son empleados para 
  //   almacenar datos con la entrada "set", estos se mantienen
  //   hasta que se hace un reset o hasta que 
  //   el sistema entra en el estado indeterminado
  //   (R=1,S=1), haciendo que el sistema se 
  //   comporte de manera aleatoria y sea imposible
  //   predecir su siguiente estado.
endmodule
