// Digital circuit Punto_3.2.dig as structural Verilog
module Punto_3_2 (
  input  J,
  input  K,
  input  c,
  output Q,
  output Q_2
);

  wire nand_1_out, nand_2_out, nand_3_out, nand_4_out, nand_5_out, nand_6_out, nand_7_out, nand_8_out,
       not_1_out, not_2_out, not_3_out, not_4_out;

  not not_1 (not_1_out, c);
  nand nand_1 (nand_1_out, J, not_1_out);
  nand nand_2 (nand_2_out, not_1_out, K);
  not not_2 (not_2_out, nand_1_out);
  not not_3 (not_3_out, nand_2_out);
  nand nand_3 (nand_3_out, Q, not_2_out);
  nand nand_4 (nand_4_out, not_3_out, Q_2);
  not not_4 (not_4_out, not_1_out);
  nand nand_5 (nand_5_out, nand_3_out, nand_6_out);
  nand nand_6 (nand_6_out, nand_5_out, nand_4_out);
  nand nand_7 (nand_7_out, nand_5_out, not_4_out);
  nand nand_8 (nand_8_out, not_4_out, nand_6_out);
  nand nand_9 (Q_2, nand_7_out, Q);
  nand nand_10 (Q, Q_2, nand_8_out);

  // Notes on the sheet:
  //   El flip flop Jk posee dos tipos de estados
  //   de entrada el J=1 cambia la salida Q =1 y K=1 
  //   cambia la salida Q'=1 en los flancos de subida,
  //   ademas posee un estado en el que no cambia la salida
  //   J=K=0 y un estado de conmutacion en que Q y Q'
  //   se alternan entre 1 ,0 y 0,1 dado por J=K=1
endmodule
