// Digital circuit punto_1.dig as structural Verilog
module punto_1 (
  input  IN0,
  input  IN1,
  input  IN2,
  input  IN3,
  input  IN4,
  input  IN5,
  input  IN6,
  input  IN7,
  input  EN4,
  input  EN2,
  input  EN1,
  output out_12
);

  wire and_1_out, and_2_out, and_3_out, and_4_out, and_5_out, and_6_out, and_7_out, and_8_out, not_1_out,
       not_2_out, not_3_out, or_1_out, or_2_out;

  not not_1 (not_1_out, EN1);
  not not_2 (not_2_out, EN2);
  not not_3 (not_3_out, EN4);
  and and_1 (and_1_out, IN0, not_1_out, not_2_out, not_3_out);
  and and_2 (and_2_out, IN1, EN1, not_2_out, not_3_out);
  and and_3 (and_3_out, IN2, not_1_out, EN2, not_3_out);
  and and_4 (and_4_out, IN3, EN1, EN2, not_3_out);
  and and_5 (and_5_out, IN4, not_1_out, not_2_out, EN4);
  and and_6 (and_6_out, IN5, EN1, EN4, not_2_out);
  and and_7 (and_7_out, IN6, not_1_out, EN2, EN4);
  and and_8 (and_8_out, IN7, EN1, EN2, EN4);
  or or_1 (or_1_out, and_1_out, and_2_out, and_3_out, and_4_out);
  or or_2 (or_2_out, and_5_out, and_6_out, and_7_out, and_8_out);
  or or_3 (out_12, or_1_out, or_2_out);
endmodule
