// Digital circuit punto_2.dig as structural Verilog
module punto_2 (
  input  EN1,
  input  EN2,
  input  IN,
  output OU0,
  output OU1,
  output OU2,
  output OU3
);

  wire not_1_out, not_2_out;

  not not_1 (not_1_out, EN2);
  not not_2 (not_2_out, EN1);
  and and_1 (OU0, not_2_out, not_1_out, IN);
  and and_2 (OU1, EN1, not_1_out, IN);
  and and_3 (OU2, not_2_out, EN2, IN);
  and and_4 (OU3, EN1, EN2, IN);
endmodule
