// Digital circuit punto_4.dig as structural Verilog
module punto_4 (
  input  D3,
  input  D2,
  input  D1,
  input  D0,
  input  enable,
  input  clear,
  input  SET,
  input  D7,
  input  D6,
  input  D5,
  input  D4,
  input  clock,
  input  enable_2,
  input  dex0,
  input  dex1,
  input  dex2,
  input  dex3,
  output s3,
  output s2,
  output s1,
  output s0,
  output ex0,
  output ex2,
  output ex2_2,
  output ex3
);

  wire d_ff_as_6_q, d_ff_as_8_q, d_ff_as_10_q, d_ff_as_12_q, driver_1_out, driver_2_out, driver_3_out,
       driver_4_out, multiplexer_1_out, multiplexer_2_out, multiplexer_3_out, multiplexer_4_out,
       multiplexer_5_out, multiplexer_6_out, multiplexer_7_out, multiplexer_8_out, multiplexer_9_out,
       multiplexer_10_out, multiplexer_11_out, multiplexer_12_out, out0, out1, out2, out3;

  Multiplexer multiplexer_1 (.sel(enable), .in_0(out3), .in_1(D3), .out(multiplexer_1_out));
  D_FF_AS d_ff_as_1 (.Set(SET), .D(multiplexer_1_out), .C(clock), .Clr(clear), .Q(out3));  // open: nQ
  Multiplexer multiplexer_2 (.sel(enable), .in_0(out2), .in_1(D2), .out(multiplexer_2_out));
  D_FF_AS d_ff_as_2 (.Set(SET), .D(multiplexer_2_out), .C(clock), .Clr(clear), .Q(out2));  // open: nQ
  Multiplexer multiplexer_3 (.sel(enable), .in_0(out1), .in_1(D1), .out(multiplexer_3_out));
  D_FF_AS d_ff_as_3 (.Set(SET), .D(multiplexer_3_out), .C(clock), .Clr(clear), .Q(out1));  // open: nQ
  Multiplexer multiplexer_4 (.sel(enable), .in_0(out0), .in_1(D0), .out(multiplexer_4_out));
  D_FF_AS d_ff_as_4 (.Set(SET), .D(multiplexer_4_out), .C(clock), .Clr(clear), .Q(out0));  // open: nQ
  assign driver_1_out = out3 ? D7 : 1'bz;  // Driver driver_1
  PullDown pulldown_1 (.out(driver_1_out));
  Multiplexer multiplexer_5 (.sel(enable_2), .in_0(s3), .in_1(driver_1_out), .out(multiplexer_5_out));
  Multiplexer multiplexer_6 (.sel(enable_2), .in_0(d_ff_as_6_q), .in_1(dex3), .out(multiplexer_6_out));
  D_FF_AS d_ff_as_5 (.Set(SET), .D(multiplexer_5_out), .C(clock), .Clr(clear), .Q(s3));  // open: nQ
  D_FF_AS d_ff_as_6 (.Set(SET), .D(multiplexer_6_out), .C(clock), .Clr(clear), .Q(d_ff_as_6_q));  // open: nQ
  assign ex3 = ~out0 ? d_ff_as_6_q : 1'bz;  // DriverInvSel driverinvsel_1
  assign driver_2_out = out2 ? D6 : 1'bz;  // Driver driver_2
  PullDown pulldown_2 (.out(driver_2_out));
  Multiplexer multiplexer_7 (.sel(enable_2), .in_0(s2), .in_1(driver_2_out), .out(multiplexer_7_out));
  Multiplexer multiplexer_8 (.sel(enable_2), .in_0(d_ff_as_8_q), .in_1(dex2), .out(multiplexer_8_out));
  D_FF_AS d_ff_as_7 (.Set(SET), .D(multiplexer_7_out), .C(clock), .Clr(clear), .Q(s2));  // open: nQ
  D_FF_AS d_ff_as_8 (.Set(SET), .D(multiplexer_8_out), .C(clock), .Clr(clear), .Q(d_ff_as_8_q));  // open: nQ
  assign ex2_2 = ~out1 ? d_ff_as_8_q : 1'bz;  // DriverInvSel driverinvsel_2
  assign driver_3_out = out1 ? D5 : 1'bz;  // Driver driver_3
  Multiplexer multiplexer_9 (.sel(enable_2), .in_0(s1), .in_1(driver_3_out), .out(multiplexer_9_out));
  Multiplexer multiplexer_10 (.sel(enable_2), .in_0(d_ff_as_10_q), .in_1(dex1), .out(multiplexer_10_out));
  PullDown pulldown_3 (.out(driver_3_out));
  D_FF_AS d_ff_as_9 (.Set(SET), .D(multiplexer_9_out), .C(clock), .Clr(clear), .Q(s1));  // open: nQ
  D_FF_AS d_ff_as_10 (.Set(SET), .D(multiplexer_10_out), .C(clock), .Clr(clear), .Q(d_ff_as_10_q));  // open: nQ
  assign driver_4_out = out0 ? D4 : 1'bz;  // Driver driver_4
  assign ex2 = ~out2 ? d_ff_as_10_q : 1'bz;  // DriverInvSel driverinvsel_3
  Multiplexer multiplexer_11 (.sel(enable_2), .in_0(s0), .in_1(driver_4_out), .out(multiplexer_11_out));
  Multiplexer multiplexer_12 (.sel(enable_2), .in_0(d_ff_as_12_q), .in_1(dex0), .out(multiplexer_12_out));
  D_FF_AS d_ff_as_11 (.Set(SET), .D(multiplexer_11_out), .C(clock), .Clr(clear), .Q(s0));  // open: nQ
  D_FF_AS d_ff_as_12 (.Set(SET), .D(multiplexer_12_out), .C(clock), .Clr(clear), .Q(d_ff_as_12_q));  // open: nQ
  assign ex0 = ~out3 ? d_ff_as_12_q : 1'bz;  // DriverInvSel driverinvsel_4

  // Notes on the sheet:
  //   Registro de Entrada/salida
  //   Registro de entrada
  //   Registro de salida
endmodule
